# Fritzing sketch diagram (saved by Fritzing 0.9.3b)
breadboards: 1

parts:
  Part1 = Arduino Uno (Rev3) - ICSP
  J1 = Piezo Speaker
  Btn1 = Adafruit Push-button Power Switch Breakout [package=THT]
  LED1 = LED - 5mm [color="Red (633nm)" package="5 mm [THT]"]
  FC-1 = Sound Sensor
  LED2 = LED - 5mm [color="Red (633nm)" package="5 mm [THT]"]
  LED3 = LED - 5mm [color="Red (633nm)" package="5 mm [THT]"]
  LED4 = LED - 5mm [color="Red (633nm)" package="5 mm [THT]"]
  R1 = Resistor [tolerance=±5% resistance=220 package="0402 [SMD]"]
  R2 = Resistor [tolerance=±5% resistance=220 package="2512 [SMD]"]
  R3 = Resistor [tolerance=±5% resistance=220 package=THT]
  R4 = Resistor [tolerance=±5% resistance=220 package=THT]
  FC-2 = Sound Sensor
  FC-3 = Sound Sensor
  FC-4 = Sound Sensor

nets:
  N1: Part1.A0, FC-3.OUT
  N2: Part1.A1, FC-4.OUT
  N3: Part1.A2, FC-2.OUT
  N4: Part1.A3, FC-1.OUT
  N5: Part1.D9_PWM, R1.Pin_1
  N6: Part1.D10_PWM/SS, R3.Pin_1
  N7: Part1.D11_PWM/MOSI, R4.Pin_1
  N8: Part1.D12/MISO, R2.Pin_1
  GND: J1.pin1, FC-1.GND, LED3.cathode, LED4.cathode, FC-2.GND
  VCC: J1.pin2, FC-1.VCC, FC-2.VCC
  VCC_2: Btn1.IN, FC-3.VCC, FC-4.VCC
  GND_2: Btn1.GND, LED1.cathode, LED2.cathode, FC-3.GND, FC-4.GND
  N9: LED1.anode, R1.Pin_0
  N10: LED2.anode, R2.Pin_0
  N11: LED3.anode, R4.Pin_0
  N12: LED4.anode, R3.Pin_0

notes:
  Microphone 1
  Microphone 2
  Microphone 3
  Microphone 4
  LED1
  LED2
  LED3
  LED4
  Button
  Active Buzzer
